# Fritzing sketch A4899WiringDiagram (saved by Fritzing 0.9.3b)
breadboards: 1

parts:
  Pololu_A1 = Pololu A4988 [package=SO16]
  C1 = Capacitor Polarized [package=cpol-radial-100uf-25v]
  Bauteil1 = Arduino Leonardo (Rev3b)
  M1 = Stepper Motor - Bipolar

nets:
  N1: Pololu_A1.ENABLE, Bauteil1.D7
  VDD: Pololu_A1.MS1, Pololu_A1.VDD, Bauteil1.5V
  N2: Pololu_A1.RESET, Pololu_A1.SLEEP
  N3: Pololu_A1.STEP, Bauteil1.D5_PWM
  N4: Pololu_A1.DIR, Bauteil1.D6_PWM/A7
  N5: Pololu_A1.GND#8, Bauteil1.GND
  N6: Pololu_A1.1B, M1.D
  N7: Pololu_A1.1A, M1.C
  N8: Pololu_A1.2A, M1.A
  N9: Pololu_A1.2B, M1.B
  N10: Pololu_A1.GND#14, C1.-
  N11: Pololu_A1.VMOT, C1.+

notes:
  12V or 24V
