# Fritzing sketch ConnectionDiagram (saved by Fritzing 0.9.3b)

parts:
  Bauteil1 = Arduino Leonardo (Rev3b)  # not connected
  Arduino_CNC_Shield_V3_00_1 = Arduino_CNC_V3.00
  M2 = Stepper Motor - Bipolar

nets:
  N1: Arduino_CNC_Shield_V3_00_1.X-MTR_'1', M2.D
  N2: Arduino_CNC_Shield_V3_00_1.X-MTR_'2', M2.B
  N3: Arduino_CNC_Shield_V3_00_1.X-MTR_'3', M2.C
  N4: Arduino_CNC_Shield_V3_00_1.X-MTR_'4', M2.A

custom parts:
  Arduino_CNC_V3.00: Protoneer Arduino CNC Shield V3.00 If using Grbl V0.9: The “A” axis can not be used (yet). The “SCL” (Arduino A5) pin is now used for 'Probing' input. The “End Stops Z+ & Z-” (Arduino D11) and “SpnEn” (Arduino D12) have been switched!
